# Fritzing sketch electrical_schematic (saved by Fritzing 1.0.5)
breadboards: 3

parts:
  Part1 = Arduino Mega 2560 (Rev3)
  R1 = Resistor [tolerance=±5% power=0.25W resistance=100 package=THT]
  R2 = Resistor [tolerance=±5% power=0.25W resistance=100 package=THT]
  R3 = Resistor [tolerance=±5% power=0.25W resistance=100 package=THT]
  R4 = Resistor [tolerance=±5% power=0.25W resistance=100 package=THT]
  R5 = Resistor [tolerance=±5% power=0.25W resistance=100 package=THT]
  R6 = Resistor [tolerance=±5% power=0.25W resistance=100 package=THT]
  R7 = Resistor [tolerance=±5% power=0.25W resistance=100 package=THT]
  R8 = Resistor [tolerance=±5% power=0.25W resistance=100 package=THT]
  R9 = Resistor [tolerance=±5% power=0.25W resistance=100 package=THT]
  R10 = Resistor [tolerance=±5% power=0.25W resistance=100 package=THT]
  R11 = Resistor [tolerance=±5% power=0.25W resistance=100 package=THT]
  R12 = Resistor [tolerance=±5% power=0.25W resistance=100 package=THT]
  R13 = Resistor [tolerance=±5% power=0.25W resistance=100 package=THT]
  R14 = Resistor [tolerance=±5% power=0.25W resistance=100 package=THT]
  R15 = Resistor [tolerance=±5% power=0.25W resistance=100 package=THT]
  R16 = Resistor [tolerance=±5% power=0.25W resistance=100 package=THT]
  TSOP4838 = TSOP312.., 314.. [package=THT]
  TSOP4839 = TSOP312.., 314.. [package=THT]
  TSOP4840 = TSOP312.., 314.. [package=THT]
  TSOP4841 = TSOP312.., 314.. [package=THT]
  TSOP4842 = TSOP312.., 314.. [package=THT]
  TSOP4843 = TSOP312.., 314.. [package=THT]
  TSOP4845 = TSOP312.., 314.. [package=THT]
  TSOP4846 = TSOP312.., 314.. [package=THT]
  TSOP4847 = TSOP312.., 314.. [package=THT]
  TSOP4848 = TSOP312.., 314.. [package=THT]
  TSOP4849 = TSOP312.., 314.. [package=THT]
  TSOP4850 = TSOP312.., 314.. [package=THT]
  TSOP4851 = TSOP312.., 314.. [package=THT]
  TSOP4852 = TSOP312.., 314.. [package=THT]
  TSOP4853 = TSOP312.., 314.. [package=THT]
  TSOP4854 = TSOP312.., 314.. [package=THT]
  C1 = Ceramic Capacitor [capacitance=100nF voltage=35V package="100 mil [THT, multilayer]"]
  R17 = Resistor [tolerance=±5% power=0.25W resistance=180 package=THT]
  R18 = Resistor [tolerance=±5% power=0.25W resistance=180 package=THT]
  R19 = Resistor [tolerance=±5% power=0.25W resistance=180 package=THT]
  R20 = Resistor [tolerance=±5% power=0.25W resistance=180 package=THT]
  R21 = Resistor [tolerance=±5% power=0.25W resistance=180 package=THT]
  R22 = Resistor [tolerance=±5% power=0.25W resistance=180 package=THT]
  R23 = Resistor [tolerance=±5% power=0.25W resistance=180 package=THT]
  R24 = Resistor [tolerance=±5% power=0.25W resistance=180 package=THT]
  R25 = Resistor [tolerance=±5% power=0.25W resistance=180 package=THT]
  R26 = Resistor [tolerance=±5% power=0.25W resistance=180 package=THT]
  R27 = Resistor [tolerance=±5% power=0.25W resistance=180 package=THT]
  R28 = Resistor [tolerance=±5% power=0.25W resistance=180 package=THT]
  R29 = Resistor [tolerance=±5% power=0.25W resistance=180 package=THT]
  R30 = Resistor [tolerance=±5% power=0.25W resistance=180 package=THT]
  R31 = Resistor [tolerance=±5% power=0.25W resistance=180 package=THT]
  R32 = Resistor [tolerance=±5% power=0.25W resistance=180 package=THT]
  D1 = LTE-302 [package=lte-302]
  D2 = LTE-302 [package=lte-302]
  D3 = LTE-302 [package=lte-302]
  D4 = LTE-302 [package=lte-302]
  D5 = LTE-302 [package=lte-302]
  D6 = LTE-302 [package=lte-302]
  D7 = LTE-302 [package=lte-302]
  D8 = LTE-302 [package=lte-302]
  D9 = LTE-302 [package=lte-302]
  D10 = LTE-302 [package=lte-302]
  D11 = LTE-302 [package=lte-302]
  D12 = LTE-302 [package=lte-302]
  D13 = LTE-302 [package=lte-302]
  D14 = LTE-302 [package=lte-302]
  D15 = LTE-302 [package=lte-302]
  D16 = LTE-302 [package=lte-302]
  Q1 = TRANSISTOR_NPN [package=to-92]
  R33 = Resistor [tolerance=±5% power=0.25W resistance=1k package=THT]
  C2 = Ceramic Capacitor [capacitance=100nF voltage=35V package="100 mil [THT, multilayer]"]
  J1 = Basic Servo
  J2 = Basic Servo
  M1 = RioRand LM2596
  C3 = Ceramic Capacitor [capacitance=220µF voltage=35V package="100 mil [THT, multilayer]"]
  Li-Ion = Battery [internal_resistance=0.1Ω]
  C4 = Ceramic Capacitor [capacitance=470µF voltage=35V package="100 mil [THT, multilayer]"]
  VCC1 = Battery block 9V [internal_resistance=0.1Ω]
  C5 = Ceramic Capacitor [capacitance=0.1µF voltage=35V package="100 mil [THT, multilayer]"]

nets:
  GND: Part1.GND, TSOP4838.GND, TSOP4839.GND, TSOP4840.GND, TSOP4841.GND, TSOP4842.GND, TSOP4843.GND, TSOP4845.GND, TSOP4846.GND, TSOP4847.GND, TSOP4848.GND, TSOP4849.GND, TSOP4850.GND, TSOP4851.GND, TSOP4852.GND, TSOP4853.GND, TSOP4854.GND, C1.0, Q1.E, C2.1, J1.gnd, J2.gnd, M1.Pin_4, C4.1, VCC1.-, C5.1
  N1: Part1.D10_PWM, R33.Pin_1
  N2: Part1.5V, TSOP4838.Vs, TSOP4839.Vs, TSOP4840.Vs, TSOP4841.Vs, TSOP4842.Vs, TSOP4843.Vs, TSOP4845.Vs, TSOP4846.Vs, TSOP4847.Vs, TSOP4848.Vs, TSOP4849.Vs, TSOP4850.Vs, TSOP4851.Vs, TSOP4852.Vs, TSOP4853.Vs, TSOP4854.Vs, C1.1
  N3: Part1.VIN, VCC1.+
  N4: Part1.D5_PWM, J2.pulse
  N5: Part1.D6_PWM, J1.pulse
  N6: Part1.D22, R1.Pin_1
  N7: Part1.D23, R2.Pin_1
  N8: Part1.D24, R3.Pin_1
  N9: Part1.D25, R4.Pin_1
  N10: Part1.D26, R5.Pin_1
  N11: Part1.D27, R6.Pin_1
  N12: Part1.D28, R7.Pin_1
  N13: Part1.D29, R8.Pin_1
  N14: Part1.D30, R16.Pin_0
  N15: Part1.D31, R10.Pin_0
  N16: Part1.D32, R11.Pin_0
  N17: Part1.D33, R12.Pin_0
  N18: Part1.D34, R13.Pin_0
  N19: Part1.D35, R14.Pin_0
  N20: Part1.D36, R15.Pin_0
  N21: Part1.D37, R9.Pin_0
  N22: R1.Pin_0, TSOP4838.Data
  N23: R2.Pin_0, TSOP4839.Data
  N24: R3.Pin_0, TSOP4842.Data
  N25: R4.Pin_0, TSOP4841.Data
  N26: R5.Pin_0, TSOP4840.Data
  N27: R6.Pin_0, TSOP4843.Data
  N28: R7.Pin_0, TSOP4846.Data
  N29: R8.Pin_0, TSOP4845.Data
  N30: R9.Pin_1, TSOP4853.Data
  N31: R10.Pin_1, TSOP4849.Data
  N32: R11.Pin_1, TSOP4848.Data
  N33: R12.Pin_1, TSOP4850.Data
  N34: R13.Pin_1, TSOP4852.Data
  N35: R14.Pin_1, TSOP4851.Data
  N36: R15.Pin_1, TSOP4854.Data
  N37: R16.Pin_1, TSOP4847.Data
  N38: R17.Pin_0, D1.A
  VCC: R17.Pin_1, R18.Pin_0, R19.Pin_0, R20.Pin_0, R21.Pin_0, R22.Pin_0, R23.Pin_0, R24.Pin_0, R25.Pin_0, R26.Pin_1, R27.Pin_1, R28.Pin_1, R29.Pin_1, R30.Pin_1, R31.Pin_1, R32.Pin_1, C2.0, J1.vcc, J2.vcc, M1.Pin_3, C4.0, C5.0
  N39: R18.Pin_1, D16.A
  N40: R19.Pin_1, D9.A
  N41: R20.Pin_1, D10.A
  N42: R21.Pin_1, D11.A
  N43: R22.Pin_1, D12.A
  N44: R23.Pin_1, D13.A
  N45: R24.Pin_1, D15.A
  N46: R25.Pin_1, D14.A
  N47: R26.Pin_0, D2.A
  N48: R27.Pin_0, D3.A
  N49: R28.Pin_0, D5.A
  N50: R29.Pin_0, D6.A
  N51: R30.Pin_0, D4.A
  N52: R31.Pin_0, D7.A
  N53: R32.Pin_0, D8.A
  N54: D1.C, D2.C, D3.C, D4.C, D5.C, D6.C, D7.C, D8.C, D9.C, D10.C, D11.C, D12.C, D13.C, D14.C, D15.C, D16.C, Q1.C
  N55: Q1.B, R33.Pin_0
  N56: M1.Pin_1, C3.0, Li-Ion.+
  N57: M1.Pin_2, Li-Ion.-
